// Logisim project Half_adder_and_full_adder.circ as structural Verilog: 1 circuit, main circuit main
module main (
  input  A_0,
  input  A,
  input  B_0,
  input  B,
  input  A_2,
  input  B_2,
  input  C_in,
  input  A_4,
  input  A_2_2,
  input  B_4,
  input  B_2_2,
  input  A_3,
  input  B_3,
  output S_0,
  output Sum,
  output Carry,
  output S_1,
  output Sum_2,
  output S_2,
  output Carry_2,
  output S_3,
  output Overflow
);

  wire and_2_out, and_3_out, and_4_out, and_5_out, and_6_out, and_7_out, and_8_out, and_9_out, and_10_out,
       or_2_out, or_3_out, xor_2_out, xor_5_out, xor_6_out, xor_7_out;

  xor xor_1 (Sum, A, B);
  and and_1 (Carry, A, B);
  xor xor_2 (xor_2_out, A_4, B_4);
  and and_2 (and_2_out, A_4, B_4);
  xor xor_3 (Sum_2, xor_2_out, C_in);
  and and_3 (and_3_out, xor_2_out, C_in);
  or or_1 (Carry_2, and_3_out, and_2_out);
  and and_4 (and_4_out, A_2, B_2);
  and and_5 (and_5_out, A_2_2, B_2_2);
  and and_6 (and_6_out, A_3, B_3);
  xor xor_4 (S_0, A_0, B_0);
  and and_7 (and_7_out, A_0, B_0);
  xor xor_5 (xor_5_out, A_2, B_2);
  xor xor_6 (xor_6_out, A_2_2, B_2_2);
  xor xor_7 (xor_7_out, A_3, B_3);
  and and_8 (and_8_out, xor_5_out, and_7_out);
  and and_9 (and_9_out, xor_6_out, or_2_out);
  and and_10 (and_10_out, xor_7_out, or_3_out);
  xor xor_8 (S_1, xor_5_out, and_7_out);
  or or_2 (or_2_out, and_8_out, and_4_out);
  xor xor_9 (S_2, xor_6_out, or_2_out);
  or or_3 (or_3_out, and_9_out, and_5_out);
  xor xor_10 (S_3, xor_7_out, or_3_out);
  or or_4 (Overflow, and_10_out, and_6_out);

  // Notes on the sheet:
  //   半加法器
  //   全加法器
  //   C_0,in=0
  //   C_1,in
  //   C_2,in
  //   C_3,in
  //   示例: 计算4位二进制数
  //   A=6=0B0110
  //   B=4=0B0100
  //   S=6+4=10=0B1010
endmodule
