// Logisim project Four_way_multiplexer.circ as structural Verilog: 1 circuit, main circuit main
module main (
  input  Sel_0,
  input  in_2,
  input  in_3,
  input  Sel_1,
  input  in_5,
  input  in_6
);

  wire not_3_out, not_4_out;
  wire [1:0] and_1_out, and_2_out, and_3_out, and_4_out, and_9_out, and_10_out, and_11_out, and_12_out,
       multiplexer_1_out, or_1_out, or_2_out;
  wire [1:1] and_5_out, and_6_out, and_7_out, and_8_out, not_1_out, not_2_out;

  not not_1 (not_1_out[1], Sel_0);
  not not_2 (not_2_out[1], Sel_1);
  assign and_1_out = 2'b00 & {2{not_2_out[1]}} & {2{not_1_out[1]}};  // AND_Gate and_1, 2 bits wide
  assign and_2_out = 2'b01 & {2{not_2_out[1]}} & {2{Sel_0}};  // AND_Gate and_2, 2 bits wide
  assign and_3_out = 2'b10 & {2{Sel_1}} & {2{not_1_out[1]}};  // AND_Gate and_3, 2 bits wide
  assign and_4_out = 2'b11 & {2{Sel_1}} & {2{Sel_0}};  // AND_Gate and_4, 2 bits wide
  assign or_1_out = and_1_out | and_2_out | and_3_out | and_4_out;  // OR_Gate or_1, 2 bits wide
  // Probe on or_1_out
  not not_3 (not_3_out, in_2);
  not not_4 (not_4_out, in_3);
  and and_5 (and_5_out[1], not_3_out, not_4_out);
  and and_6 (and_6_out[1], in_2, not_4_out);
  and and_7 (and_7_out[1], not_3_out, in_3);
  and and_8 (and_8_out[1], in_2, in_3);
  assign and_9_out = 2'b00 & {2{and_5_out[1]}};  // AND_Gate and_9, 2 bits wide
  assign and_10_out = 2'b01 & {2{and_6_out[1]}};  // AND_Gate and_10, 2 bits wide
  assign and_11_out = 2'b10 & {2{and_7_out[1]}};  // AND_Gate and_11, 2 bits wide
  assign and_12_out = 2'b11 & {2{and_8_out[1]}};  // AND_Gate and_12, 2 bits wide
  // Probe on or_2_out
  assign or_2_out = and_9_out | and_10_out | and_11_out | and_12_out;  // OR_Gate or_2, 2 bits wide
  Multiplexer #(.select(2), .width(2), .enable("false")) multiplexer_1 (
    .in0(2'b00), .in1(2'b01), .in2(2'b10), .in3(2'b11), .out(multiplexer_1_out), .sel({in_6, in_5}));
  // Probe on multiplexer_1_out

  // Notes on the sheet:
  //   A
  //   B
  //   C
  //   D
  //   与2位数据宽度的逻辑门保持兼容
  //   OUT
  //   等价于->
  //   多路复用器
endmodule
