// Logisim project Logic_gate_implemented_by_mosfet.circ as structural Verilog: 1 circuit, main circuit main
module main (
  input  in_1,
  input  in_2,
  input  in_3,
  input  in_4,
  input  in_5,
  input  in_6,
  output out_7,
  output out_8,
  output out_9,
  output out_10,
  output out_11,
  output out_12,
  output out_13,
  output out_14,
  output out_15,
  output out_16
);

  wire transistor_6_out, transistor_7_out, transistor_11_out, transistor_26_out, transistor_27_out;

  Transistor #(.\type ("n")) transistor_1 (.in(1'b1), .out(out_7), .gate(in_1));
  Transistor transistor_2 (.in(1'b0), .out(out_7), .gate(in_1));
  Transistor transistor_3 (.in(1'b1), .out(out_10), .gate(in_2));
  Transistor #(.gate("br")) transistor_4 (.in(1'b1), .out(out_10), .gate(in_1));
  Transistor #(.\type ("n")) transistor_5 (.in(transistor_6_out), .out(out_10), .gate(in_1));
  Transistor #(.\type ("n")) transistor_6 (.in(1'b0), .out(transistor_6_out), .gate(in_2));
  Transistor transistor_7 (.in(1'b1), .out(transistor_7_out), .gate(in_1));
  Transistor transistor_8 (.in(transistor_7_out), .out(out_14), .gate(in_2));
  Transistor #(.\type ("n"), .gate("br")) transistor_9 (.in(1'b0), .out(out_14), .gate(in_2));
  Transistor #(.\type ("n")) transistor_10 (.in(1'b0), .out(out_14), .gate(in_1));
  Transistor transistor_11 (.in(1'b1), .out(transistor_11_out), .gate(in_1));
  Transistor #(.\type ("n")) transistor_12 (.in(1'b0), .out(transistor_11_out), .gate(in_1));
  Transistor transistor_13 (.in(in_1), .out(out_15), .gate(in_2));
  Transistor #(.\type ("n")) transistor_14 (.in(transistor_11_out), .out(out_15), .gate(in_2));
  Transistor transistor_15 (.in(1'b1), .out(out_8), .gate(in_1));
  Transistor #(.\type ("n")) transistor_16 (.in(1'b0), .out(out_8), .gate(in_1));
  Transistor transistor_17 (.in(1'b1), .out(out_9), .gate(out_10));
  Transistor #(.\type ("n")) transistor_18 (.in(1'b0), .out(out_9), .gate(out_10));
  Transistor transistor_19 (.in(1'b1), .out(out_12), .gate(out_14));
  Transistor #(.\type ("n")) transistor_20 (.in(1'b0), .out(out_12), .gate(out_14));
  Transistor transistor_21 (.in(1'b1), .out(out_16), .gate(out_15));
  Transistor #(.\type ("n")) transistor_22 (.in(1'b0), .out(out_16), .gate(out_15));
  Transistor #(.\type ("n")) transistor_23 (.in(1'b1), .out(out_11), .gate(in_3));
  Transistor #(.\type ("n"), .gate("br")) transistor_24 (.in(1'b1), .out(out_11), .gate(in_5));
  Transistor transistor_25 (.in(transistor_26_out), .out(out_11), .gate(in_3));
  Transistor transistor_26 (.in(1'b0), .out(transistor_26_out), .gate(in_5));
  Transistor transistor_27 (.in(1'b1), .out(transistor_27_out), .gate(in_6));
  Transistor #(.\type ("n")) transistor_28 (.in(1'b0), .out(out_13), .gate(in_6));
  Transistor #(.\type ("n"), .gate("br")) transistor_29 (.in(1'b0), .out(out_13), .gate(in_4));
  Transistor transistor_30 (.in(transistor_27_out), .out(out_13), .gate(in_4));

  // Notes on the sheet:
  //   非门
  //   缓冲器
  //   与门(与非门+非门)
  //   与非门
  //   或门(或非门+非门)
  //   或非门
  //   异或门
  //   同或门(异或门+非门)
endmodule
