// Logisim project Program_Counter.circ as structural Verilog: 1 circuit, main circuit main
module main (
);

  wire clock_1_out;
  wire [31:0] adder_1_out, PC_q;

  Clock clock_1 (.out(clock_1_out));
  Adder #(.width(32)) adder_1 (.a(PC_q), .b(32'h4), .out(adder_1_out));  // open: cin, cout
  Register #(.width(32)) PC (.D(adder_1_out), .en(1'b1), .clk(clock_1_out), .Q(PC_q));  // open: clr
  RAM #(.addrWidth(24), .dataWidth(32), .trigger("high"), .databus("bibus")) IMEN (.addr(PC_q[25:2]));  // open: we, oe, clk, din, dout

  // Notes on the sheet:
  //   PC地址->实际内存地址, 只需要滤掉二进制的前两位
endmodule
