// Logisim project RAM_example.circ as structural Verilog: 1 circuit, main circuit main
module main (
  input  in_1,
  input  \写入模式 ,
  input  in_3,
  input  \输出模式 ,
  input  \选一个地址 ,
  input  in_6
);

  wire clock_1_out;
  wire [23:0] and_1_out, and_2_out, and_3_out, bit_extender_1_out, bit_extender_2_out, bit_extender_3_out,
       or_1_out;
  wire [31:0] ram_1_data;

  assign bit_extender_1_out = {{23{in_1}}, in_1};  // Bit_Extender bit_extender_1
  assign bit_extender_2_out = {{23{\选一个地址 }}, \选一个地址 };  // Bit_Extender bit_extender_2
  assign bit_extender_3_out = {{23{in_6}}, in_6};  // Bit_Extender bit_extender_3
  assign and_1_out = bit_extender_1_out & {24{1'b0}};  // AND_Gate and_1, 24 bits wide
  assign and_2_out = bit_extender_2_out & 24'h1;  // AND_Gate and_2, 24 bits wide
  assign and_3_out = bit_extender_3_out & 24'h2;  // AND_Gate and_3, 24 bits wide
  assign or_1_out = and_1_out | and_2_out | and_3_out;  // OR_Gate or_1, 24 bits wide
  RAM #(.addrWidth(24), .dataWidth(32)) ram_1 (
    .addr(or_1_out), .we(\写入模式 ), .oe(\输出模式 ), .clk(clock_1_out), .data(ram_1_data));
  Clock clock_1 (.out(clock_1_out));
  Transistor #(.\type ("n"), .width(32)) transistor_1 (.in(32'h66666666), .out(ram_1_data), .gate(in_3));
  // Probe on ram_1_data
endmodule
