// Logisim project Registers.circ as structural Verilog: 1 circuit, main circuit main
module main (
  input  S,
  input  in_2,
  input  in_3,
  input  R,
  input  D,
  input  in_6,
  input  D_2,
  input  in_8,
  input  in_9,
  input  E,
  output out_11,
  output out_12,
  output out_13,
  output out_14,
  output Q,
  output out_16,
  output out_17,
  output _Q,
  output Q_2,
  output out_20,
  output _Q_2
);

  wire and_1_out, and_2_out, and_3_out, buffer_1_out, buffer_2_out, clock_1_out, clock_2_out, clock_3_out,
       clock_4_out, clock_5_out, clock_6_out, nand_1_out, nand_2_out, nand_5_out, nand_6_out, nand_7_out,
       nand_8_out, not_1_out, not_2_out;

  Clock clock_1 (.out(clock_1_out));
  Clock clock_2 (.out(clock_2_out));
  buf buffer_1 (buffer_1_out, clock_3_out);
  Clock clock_3 (.out(clock_3_out));
  nand nand_1 (nand_1_out, S, clock_1_out);
  nand nand_2 (nand_2_out, clock_1_out, R);
  buf buffer_2 (buffer_2_out, clock_2_out);
  not not_1 (not_1_out, buffer_2_out);
  not not_2 (not_2_out, buffer_1_out);
  and and_1 (and_1_out, not_2_out, clock_3_out);
  nand nand_3 (out_11, nand_1_out, out_14);
  nand nand_4 (out_14, out_11, nand_2_out);
  and and_2 (and_2_out, not_1_out, clock_2_out);
  and and_3 (and_3_out, E, and_1_out);
  nand nand_5 (nand_5_out, D, and_2_out);
  nand nand_6 (nand_6_out, nand_5_out, and_2_out);
  nand nand_7 (nand_7_out, D_2, and_3_out);
  nand nand_8 (nand_8_out, nand_7_out, and_3_out);
  nand nand_9 (Q, nand_5_out, _Q);
  nand nand_10 (_Q, Q, nand_6_out);
  nand nand_11 (Q_2, nand_7_out, _Q_2);
  nand nand_12 (_Q_2, Q_2, nand_8_out);
  Clock clock_4 (.out(clock_4_out));
  Clock clock_5 (.out(clock_5_out));
  Register #(.width(1)) register_1 (.D(in_8), .en(in_9), .clk(clock_6_out), .Q(out_20));  // open: clr
  Clock clock_6 (.out(clock_6_out));
  S_R_Flip_Flop s_r_ff_1 (.S(in_2), .R(in_3), .clk(clock_4_out), .Q(out_12), .Qn(out_13));  // open: reset, preset
  D_Flip_Flop d_ff_1 (.D(in_6), .clk(clock_5_out), .Q(out_16), .Qn(out_17));  // open: preset, reset

  // Notes on the sheet:
  //   CLK
  //   寄存器
  //   CLK
  //   S-R 触发器
  //   DQ 触发器
endmodule
