// Logisim project risv_v_simple.circ as structural Verilog: 6 circuits, main circuit main
module main (
);

  wire ASel, BrEq, BrLt, BrUn, BSel, clock_1_out, clock_2_out, clock_3_out, clock_4_out, MemRW, PCSel, RegWEn;
  wire [1:0] WBSel;
  wire [2:0] func3;
  wire [3:0] ALUSel;
  wire [4:0] bit_extender_1_out, ImmSel, multiplier_1_out, rd, rs1, rs2;
  wire [6:0] func7, opcode;
  wire [31:0] adder_1_out, alu_1_out_4, bit_extender_2_out, bit_extender_3_out, imm_gen_1_out_3,
       multiplexer_1_out, multiplexer_2_out, multiplexer_3_out, multiplexer_4_out, multiplexer_5_out,
       ram_2_dout, reg_file_1_rs1_output, reg_file_1_rs2_output, register_1_q, shifter_1_out;

  Adder #(.width(32)) adder_1 (.a(register_1_q), .b(32'h4), .out(adder_1_out));  // open: cin, cout
  Register #(.width(32)) register_1 (.D(multiplexer_1_out), .en(1'b1), .clk(clock_1_out), .Q(register_1_q), .clr(1'b0));
  Multiplexer #(.width(32), .enable("false")) multiplexer_1 (
    .in0(adder_1_out), .in1(alu_1_out_4), .out(multiplexer_1_out), .sel(PCSel));
  Clock clock_1 (.out(clock_1_out));
  Clock clock_2 (.out(clock_2_out));
  RAM #(.addrWidth(24), .dataWidth(32)) ram_1 (
    .addr(register_1_q[25:2]), .we(1'b0), .oe(1'b1), .clk(clock_2_out),
    .data({func7, rs2, rs1, func3, rd, opcode}));
  Multiplexer #(.select(2), .width(32), .enable("false")) multiplexer_2 (
    .in0(alu_1_out_4), .in1(multiplexer_5_out), .in2(register_1_q), .out(multiplexer_2_out), .sel(WBSel));  // open: in3
  control_unit control_unit_1 (
    .ASel(ASel), .ImmSel(ImmSel), .PCSel(PCSel), .BrEq(BrEq), .BrLt(BrLt), .RegWEn(RegWEn), .BrUn(BrUn),
    .BSel(BSel), .inst({func7, rs2, rs1, func3, rd, opcode}), .ALUSel(ALUSel), .MemRW(MemRW), .WBSel(WBSel));
  reg_file reg_file_1 (
    .rs1_input(rs1), .rs2_input(rs2), .rd(rd), .wb(multiplexer_2_out), .RegWEn(RegWEn), .Clock(clock_3_out),
    .rs1_output(reg_file_1_rs1_output), .rs2_output(reg_file_1_rs2_output));
  Clock clock_3 (.out(clock_3_out));
  imm_gen imm_gen_1 (.out_3(imm_gen_1_out_3), .in_1(ImmSel), .in_2({func7, rs2, rs1, func3, rd, opcode}));
  branch_comp branch_comp_1 (
    .in_3(BrUn), .out_5(BrLt), .in_1(reg_file_1_rs1_output), .in_2(reg_file_1_rs2_output), .out_4(BrEq));
  Multiplexer #(.width(32), .enable("false")) multiplexer_3 (
    .in0(reg_file_1_rs1_output), .in1(register_1_q), .out(multiplexer_3_out), .sel(ASel));
  Multiplexer #(.width(32), .enable("false")) multiplexer_4 (
    .in0(reg_file_1_rs2_output), .in1(imm_gen_1_out_3), .out(multiplexer_4_out), .sel(BSel));
  ALU alu_1 (.in_3(ALUSel), .in_2(multiplexer_4_out), .in_1(multiplexer_3_out), .out_4(alu_1_out_4));
  Clock clock_4 (.out(clock_4_out));
  RAM #(.addrWidth(14), .dataWidth(32), .trigger("falling"), .databus("bibus")) ram_2 (
    .addr(alu_1_out_4[15:2]), .we(MemRW), .oe(1'b1), .clk(clock_4_out), .din(reg_file_1_rs2_output),
    .dout(ram_2_dout));
  assign bit_extender_1_out = {{3{1'b0}}, alu_1_out_4[1:0]};  // Bit_Extender bit_extender_1
  Multiplier #(.width(5)) multiplier_1 (
    .a(bit_extender_1_out), .b(5'b01110), .out(multiplier_1_out));  // open: cin, cout
  Shifter #(.width(32), .shift("lr")) shifter_1 (.in(ram_2_dout), .\dist (multiplier_1_out), .out(shifter_1_out));
  assign bit_extender_2_out = {{24{shifter_1_out[7]}}, shifter_1_out[7:0]};  // Bit_Extender bit_extender_2
  assign bit_extender_3_out = {{16{shifter_1_out[15]}}, shifter_1_out[15:0]};  // Bit_Extender bit_extender_3
  Multiplexer #(.select(3), .width(32), .enable("false")) multiplexer_5 (
    .in0(bit_extender_2_out), .in1(bit_extender_3_out), .in2(shifter_1_out), .out(multiplexer_5_out),
    .sel(func3));  // open: in3, in4, in5, in6, in7

  // Notes on the sheet:
  //   PC输出线
  //   输出到PC自己, Reg File, ALU的A端口
  //   控制单元
  //   Write Back输出线
  //   ALU输出线
  //   从ALU输出到PC或别的寄存器或WB
  //   Write Back意思是从内存写入寄存器
  //   是否以无符号模式比较
  //   0 从rs1输入, 1 从PC输入
  //   0 从rs2输入, 1 从立即数输入
  //   alu模式
  //   DRAM读写
  //   0 PC继续自增, 1 PC改为ALU的输出值
  //   寄存器允许写入
  //   因为不同的指令类型imm有分段
  //   0 从alu输入, 1 从wb输入, 2 从PC输入
  //   到ALU
  //   到Reg File
  //   所以根据对应的指令type进行对应的解析处理
  //   rs2(即B)具有保存到数据内存中的能力
  //   数据内存下降沿更新
endmodule

module reg_file (
  input  [4:0] rs1_input,
  input  [4:0] rs2_input,
  input  [4:0] rd,
  input  [31:0] wb,
  input  RegWEn,
  input  Clock,
  output [31:0] rs1_output,
  output [31:0] rs2_output
);

  wire and_1_out, and_2_out, and_3_out, and_4_out, and_5_out, and_6_out, and_7_out, and_8_out,
       decoder_1_out1, decoder_1_out2, decoder_1_out5, decoder_1_out6, decoder_1_out7, decoder_1_out8,
       decoder_1_out9, decoder_1_out10;
  wire [31:0] a0, ra, s0, s1, sp, t0, t1, t2;

  Decoder #(.select(5), .enable("false")) decoder_1 (
    .out1(decoder_1_out1), .out2(decoder_1_out2), .out5(decoder_1_out5), .out6(decoder_1_out6),
    .out7(decoder_1_out7), .out8(decoder_1_out8), .out9(decoder_1_out9), .out10(decoder_1_out10), .sel(rd));  // open: out0, out3, out4, out11, out12, out13, out14, out15, out16, out17, out18, out19, out20, out21, out22, out23, out24, out25, out26, out27, out28, out29, out30, out31
  and and_1 (and_1_out, decoder_1_out1, RegWEn);
  and and_2 (and_2_out, decoder_1_out2, RegWEn);
  and and_3 (and_3_out, decoder_1_out5, RegWEn);
  and and_4 (and_4_out, decoder_1_out6, RegWEn);
  and and_5 (and_5_out, decoder_1_out7, RegWEn);
  and and_6 (and_6_out, decoder_1_out8, RegWEn);
  and and_7 (and_7_out, decoder_1_out9, RegWEn);
  and and_8 (and_8_out, decoder_1_out10, RegWEn);
  Register #(.width(32)) register_1 (.D(wb), .en(and_1_out), .clk(Clock), .Q(ra));  // open: clr
  Register #(.width(32)) register_2 (.D(wb), .en(and_2_out), .clk(Clock), .Q(sp));  // open: clr
  Register #(.width(32)) register_3 (.D(wb), .en(and_3_out), .clk(Clock), .Q(t0));  // open: clr
  Register #(.width(32)) register_4 (.D(wb), .en(and_4_out), .clk(Clock), .Q(t1));  // open: clr
  Register #(.width(32)) register_5 (.D(wb), .en(and_5_out), .clk(Clock), .Q(t2));  // open: clr
  Register #(.width(32)) register_6 (.D(wb), .en(and_6_out), .clk(Clock), .Q(s0));  // open: clr
  Register #(.width(32)) register_7 (.D(wb), .en(and_7_out), .clk(Clock), .Q(s1));  // open: clr
  Register #(.width(32)) register_8 (.D(wb), .en(and_8_out), .clk(Clock), .Q(a0));  // open: clr
  Multiplexer #(.select(5), .width(32), .enable("false")) multiplexer_1 (
    .in0({32{1'b0}}), .in1(ra), .in2(sp), .in5(t0), .in6(t1), .in7(t2), .in8(s0), .in9(s1), .in10(a0),
    .out(rs1_output), .sel(rs2_input));  // open: in3, in4, in11, in12, in13, in14, in15, in16, in17, in18, in19, in20, in21, in22, in23, in24, in25, in26, in27, in28, in29, in30, in31
  Multiplexer #(.select(5), .width(32), .enable("false")) multiplexer_2 (
    .in0({32{1'b0}}), .in1(ra), .in2(sp), .in5(t0), .in6(t1), .in7(t2), .in8(s0), .in9(s1), .in10(a0),
    .out(rs2_output), .sel(rs1_input));  // open: in3, in4, in11, in12, in13, in14, in15, in16, in17, in18, in19, in20, in21, in22, in23, in24, in25, in26, in27, in28, in29, in30, in31

  // Other names for the same wires on the sheet: clk = Clock; read_data1[31:0] = rs1_output;
  //   read_data2[31:0] = rs2_output; read_reg1[4:0] = rs1_input; read_reg2[4:0] = rs2_input; write_data[31:0] = wb;
  //   write_en = RegWEn; write_reg[4:0] = rd
endmodule

module ALU (
  input  [31:0] in_1,
  input  [31:0] in_2,
  input  [3:0] in_3,
  output [31:0] out_4
);

  wire comparator_2_lt, xor_2_out;
  wire [31:0] adder_1_out, and_1_out, bit_extender_1_out, divider_1_out, divider_1_rem, multiplexer_1_out,
       multiplexer_2_out, multiplexer_4_out, multiplier_1_cout, multiplier_1_out, multiplier_2_cout,
       negator_1_out, negator_2_out, not_1_out, or_1_out, shifter_1_out, shifter_2_out, shifter_3_out,
       xor_1_out;

  Comparator comparator_1 ();  // open: a, b, gt, eq, lt
  Adder #(.width(32)) adder_1 (.a(in_1), .b(in_2), .out(adder_1_out));  // open: cin, cout
  assign and_1_out = in_1 & in_2;  // AND_Gate and_1, 32 bits wide
  assign or_1_out = in_1 | in_2;  // OR_Gate or_1, 32 bits wide
  assign xor_1_out = in_1 ^ in_2;  // XOR_Gate xor_1, 32 bits wide
  Shifter #(.width(32), .shift("lr")) shifter_1 (.in(in_1), .\dist (in_2[4:0]), .out(shifter_1_out));
  Shifter #(.width(32), .shift("ar")) shifter_2 (.in(in_1), .\dist (in_2[4:0]), .out(shifter_2_out));
  Shifter #(.width(32)) shifter_3 (.in(in_1), .\dist (in_2[4:0]), .out(shifter_3_out));
  Comparator #(.width(32)) comparator_2 (.a(in_1), .b(in_2), .lt(comparator_2_lt));  // open: gt, eq
  Divider #(.width(32)) divider_1 (.a(in_1), .b(in_2), .out(divider_1_out), .rem(divider_1_rem));  // open: upper
  Multiplier #(.width(32)) multiplier_1 (
    .a(in_1), .b(in_2), .out(multiplier_1_out), .cout(multiplier_1_cout));  // open: cin
  Subtractor #(.width(32)) subtractor_1 (.a(in_1), .b(in_2));  // open: out, bin, bout
  Negator #(.width(32)) negator_1 (.in(in_2), .out(negator_1_out));
  Negator #(.width(32)) negator_2 (.in(in_1), .out(negator_2_out));
  assign bit_extender_1_out = {{31{1'b0}}, comparator_2_lt};  // Bit_Extender bit_extender_1
  Multiplexer #(.width(32), .enable("false")) multiplexer_1 (
    .in0(in_2), .in1(negator_1_out), .out(multiplexer_1_out), .sel(in_2[31]));
  Multiplexer #(.width(32), .enable("false")) multiplexer_2 (
    .in0(in_1), .in1(negator_2_out), .out(multiplexer_2_out), .sel(in_1[31]));
  xor xor_2 (xor_2_out, in_2[31], in_1[31]);
  Multiplier #(.width(32)) multiplier_2 (
    .a(multiplexer_1_out), .b(multiplexer_2_out), .cout(multiplier_2_cout));  // open: out, cin
  assign not_1_out = ~multiplier_2_cout;  // NOT_Gate not_1, 32 bits wide
  Multiplexer #(.select(4), .width(32), .enable("false")) multiplexer_3 (
    .in0(adder_1_out), .in1(and_1_out), .in2(or_1_out), .in3(xor_1_out), .in4(shifter_1_out),
    .in5(shifter_2_out), .in6(shifter_3_out), .in7(bit_extender_1_out), .in8(divider_1_out),
    .in9(divider_1_rem), .in10(multiplier_1_out), .in11(multiplier_1_cout), .in12(in_2), .out(out_4),
    .sel(in_3));  // open: in13, in14, in15
  Multiplexer #(.width(32), .enable("false")) multiplexer_4 (
    .in0(multiplier_2_cout), .in1(not_1_out), .out(multiplexer_4_out), .sel(xor_2_out));
  // AND_Gate and_2 has open pins: in0=multiplexer_4_out, out=open

  // Other names for the same wires on the sheet: A[31:0] = in_1; ALUSel[3:0] = in_3; B[31:0] = in_2;
  //   result[31:0] = out_4

  // Notes on the sheet:
  //   如果是负数先转换为正数
  //   如果有一个数是负数
  //   那就按位取反
endmodule

module imm_gen (
  input  [4:0] in_1,
  input  [31:0] in_2,
  output [31:0] out_3
);

  wire [31:0] and_1_out, and_2_out, and_3_out, and_4_out, and_5_out, bit_extender_1_out, bit_extender_2_out,
       bit_extender_3_out, bit_extender_4_out, bit_extender_5_out, bit_extender_6_out, bit_extender_7_out,
       bit_extender_8_out, bit_extender_9_out;

  assign bit_extender_1_out = {{31{in_1[0]}}, in_1[0]};  // Bit_Extender bit_extender_1
  assign bit_extender_2_out = {{20{in_2[31]}}, in_2[31:20]};  // Bit_Extender bit_extender_2
  assign bit_extender_3_out = {{31{in_1[1]}}, in_1[1]};  // Bit_Extender bit_extender_3
  assign bit_extender_4_out = {{20{in_2[31]}}, {in_2[31:25], in_2[11:7]}};  // Bit_Extender bit_extender_4
  assign bit_extender_5_out = {{31{in_1[2]}}, in_1[2]};  // Bit_Extender bit_extender_5
  assign bit_extender_6_out = {{19{in_2[31]}}, {in_2[31], in_2[7], in_2[30:25], in_2[11:8], 1'b0}};  // Bit_Extender bit_extender_6
  assign bit_extender_7_out = {{31{in_1[3]}}, in_1[3]};  // Bit_Extender bit_extender_7
  assign bit_extender_8_out = {{31{in_1[4]}}, in_1[4]};  // Bit_Extender bit_extender_8
  assign bit_extender_9_out = {{11{in_2[31]}}, {in_2[31], in_2[19:12], in_2[20], in_2[30:21], 1'b0}};  // Bit_Extender bit_extender_9
  assign and_1_out = bit_extender_1_out & bit_extender_2_out;  // AND_Gate and_1, 32 bits wide
  assign and_2_out = bit_extender_3_out & bit_extender_4_out;  // AND_Gate and_2, 32 bits wide
  assign and_3_out = bit_extender_5_out & bit_extender_6_out;  // AND_Gate and_3, 32 bits wide
  assign and_4_out = bit_extender_7_out & {in_2[31:12], {12{1'b0}}};  // AND_Gate and_4, 32 bits wide
  assign and_5_out = bit_extender_8_out & bit_extender_9_out;  // AND_Gate and_5, 32 bits wide
  assign out_3 = and_1_out | and_2_out | and_3_out | and_4_out | and_5_out;  // OR_Gate or_1, 32 bits wide

  // Other names for the same wires on the sheet: instruction[31:0] = in_2; immediate_select[4:0] = in_1;
  //   immediate_value[31:0] = out_3

  // Notes on the sheet:
  //   因为SB类型没有捕获imm的0位, 所以手动补0
  //   根据Core Instruction Formats来设计
  //   I类型指令
  //   20-31 imm
  //   R类型指令
  //   7-11 rd
  //   25-31 func7
  //   SB类型指令
  //   内容较多, 具体看CIF表
  //   U类型指令
  //   参考上面SB的解释
  //   UJ类型指令
  //   整合后0-4 rd, 5-11 func7
endmodule

module branch_comp (
  input  [31:0] in_1,
  input  [31:0] in_2,
  input  in_3,
  output out_4,
  output out_5
);

  wire comparator_1_eq, comparator_1_lt, comparator_2_eq, comparator_2_lt;

  Comparator #(.width(32)) comparator_1 (.a(in_1), .b(in_2), .eq(comparator_1_eq), .lt(comparator_1_lt));  // open: gt
  Comparator #(.width(32), .mode("unsigned")) comparator_2 (
    .a(in_1), .b(in_2), .eq(comparator_2_eq), .lt(comparator_2_lt));  // open: gt
  Multiplexer #(.enable("false")) multiplexer_1 (.in0(comparator_1_eq), .in1(comparator_2_eq), .out(out_4), .sel(in_3));
  Multiplexer #(.enable("false")) multiplexer_2 (.in0(comparator_1_lt), .in1(comparator_2_lt), .out(out_5), .sel(in_3));

  // Other names for the same wires on the sheet: A[31:0] = in_1; B[31:0] = in_2; branch_equal = out_4;
  //   branch_less_than = out_5; branch_unsigned = in_3

  // Notes on the sheet:
  //   signed
  //   unsigned
endmodule

module control_unit (
  input  [31:0] inst,
  input  BrEq,
  input  BrLt,
  output PCSel,
  output RegWEn,
  output [4:0] ImmSel,
  output BrUn,
  output ASel,
  output BSel,
  output [3:0] ALUSel,
  output MemRW,
  output [1:0] WBSel
);

  wire add, addi, and_1_out, and_2_out, and_3_out, and_4_out, and_1080616f, andi, beq, blt, bne,
       comparator_9_eq, comparator_10_eq, comparator_11_eq, comparator_12_eq, comparator_13_eq,
       comparator_14_eq, comparator_15_eq, comparator_16_eq, comparator_17_eq, comparator_18_eq,
       comparator_19_eq, div, divu, I, I_jalr, I_Load, lb, lh, lw, mul, mulh, mulhu, or_3_out, or_4_out,
       or_5_out, or_6_out, or_7_out, or_8_out, or_9_out, or_10_out, or_11_out, or_12_out, or_483976f9, ori,
       R, rem_90254230, remu, sll_a5a2ae92, slli, slt, slti, srai, srl_04da4a0d, srli, sub, xor_e25a1cfa,
       xori;
  wire [1:0] and_35_out, and_36_out, and_37_out, bit_extender_15_out, bit_extender_16_out,
       bit_extender_17_out;
  wire [3:0] and_38_out, and_39_out, and_40_out, and_41_out, and_42_out, and_43_out, and_44_out, and_45_out,
       and_46_out, and_47_out, and_48_out, and_49_out, and_50_out, and_51_out, bit_extender_1_out,
       bit_extender_2_out, bit_extender_3_out, bit_extender_4_out, bit_extender_5_out, bit_extender_6_out,
       bit_extender_7_out, bit_extender_8_out, bit_extender_9_out, bit_extender_10_out, bit_extender_11_out,
       bit_extender_12_out, bit_extender_13_out, bit_extender_14_out;

  Comparator #(.width(7)) comparator_1 (.a(inst[6:0]), .b(7'b0110011), .eq(R));  // open: gt, lt
  Comparator #(.width(7)) comparator_2 (.a(inst[6:0]), .b(7'b0000011), .eq(I_Load));  // open: gt, lt
  Comparator #(.width(7)) comparator_3 (.a(inst[6:0]), .b(7'b0010011), .eq(I));  // open: gt, lt
  Comparator #(.width(7)) comparator_4 (.a(inst[6:0]), .b(7'b0100011), .eq(ImmSel[1]));  // open: gt, lt
  Comparator #(.width(7)) comparator_5 (.a(inst[6:0]), .b(7'b1100011), .eq(ImmSel[2]));  // open: gt, lt
  Comparator #(.width(7)) comparator_6 (.a(inst[6:0]), .b(7'b0110111), .eq(ImmSel[3]));  // open: gt, lt
  Comparator #(.width(7)) comparator_7 (.a(inst[6:0]), .b(7'b1101111), .eq(ImmSel[4]));  // open: gt, lt
  Comparator #(.width(7)) comparator_8 (.a(inst[6:0]), .b(7'b1100111), .eq(I_jalr));  // open: gt, lt
  Comparator #(.width(3), .mode("unsigned")) comparator_9 (
    .a(inst[14:12]), .b(3'b000), .eq(comparator_9_eq));  // open: gt, lt
  Comparator #(.width(3), .mode("unsigned")) comparator_10 (
    .a(inst[14:12]), .b(3'b001), .eq(comparator_10_eq));  // open: gt, lt
  Comparator #(.width(3), .mode("unsigned")) comparator_11 (
    .a(inst[14:12]), .b(3'b010), .eq(comparator_11_eq));  // open: gt, lt
  Comparator #(.width(3), .mode("unsigned")) comparator_12 (
    .a(inst[14:12]), .b(3'b011), .eq(comparator_12_eq));  // open: gt, lt
  Comparator #(.width(3), .mode("unsigned")) comparator_13 (
    .a(inst[14:12]), .b(3'b100), .eq(comparator_13_eq));  // open: gt, lt
  Comparator #(.width(3), .mode("unsigned")) comparator_14 (
    .a(inst[14:12]), .b(3'b101), .eq(comparator_14_eq));  // open: gt, lt
  Comparator #(.width(3), .mode("unsigned")) comparator_15 (
    .a(inst[14:12]), .b(3'b110), .eq(comparator_15_eq));  // open: gt, lt
  Comparator #(.width(3), .mode("unsigned")) comparator_16 (
    .a(inst[14:12]), .b(3'b111), .eq(comparator_16_eq));  // open: gt, lt
  Comparator #(.width(7), .mode("unsigned")) comparator_17 (
    .a(inst[31:25]), .b({7{1'b0}}), .eq(comparator_17_eq));  // open: gt, lt
  Comparator #(.width(7), .mode("unsigned")) comparator_18 (
    .a(inst[31:25]), .b(7'b0000001), .eq(comparator_18_eq));  // open: gt, lt
  Comparator #(.width(7), .mode("unsigned")) comparator_19 (
    .a(inst[31:25]), .b(7'b0100000), .eq(comparator_19_eq));  // open: gt, lt
  and and_1 (and_1_out, BrEq, beq);
  and and_2 (and_2_out, ~BrEq, bne);  // AND_Gate
  and and_3 (and_3_out, BrLt, blt);
  and and_4 (and_4_out, BrLt, BrUn);
  or or_1 (PCSel, and_1_out, and_2_out, and_3_out, and_4_out, ImmSel[4], I_jalr);
  and and_5 (add, R, comparator_9_eq, comparator_17_eq);
  and and_6 (mul, R, comparator_9_eq, comparator_18_eq);
  and and_7 (sub, R, comparator_9_eq, comparator_19_eq);
  and and_8 (sll_a5a2ae92, R, comparator_10_eq, comparator_17_eq);
  and and_9 (mulh, R, comparator_10_eq, comparator_18_eq);
  and and_10 (slt, R, comparator_11_eq, comparator_17_eq);
  and and_11 (mulhu, R, comparator_12_eq, comparator_18_eq);
  and and_12 (xor_e25a1cfa, R, comparator_13_eq, comparator_17_eq);
  and and_13 (div, R, comparator_13_eq, comparator_18_eq);
  and and_14 (divu, R, comparator_14_eq, comparator_18_eq);
  and and_15 (srl_04da4a0d, R, comparator_14_eq, comparator_17_eq);
  and and_16 (or_483976f9, R, comparator_15_eq, comparator_17_eq);
  and and_17 (rem_90254230, R, comparator_15_eq, comparator_18_eq);
  and and_18 (remu, R, comparator_16_eq, comparator_18_eq);
  and and_19 (and_1080616f, R, comparator_16_eq, comparator_17_eq);
  and and_20 (lb, I_Load, comparator_9_eq);
  and and_21 (lh, I_Load, comparator_10_eq);
  and and_22 (lw, I_Load, comparator_11_eq);
  and and_23 (addi, I, comparator_9_eq);
  and and_24 (slli, I, comparator_10_eq, comparator_17_eq);
  and and_25 (slti, I, comparator_11_eq);
  and and_26 (xori, I, comparator_13_eq);
  and and_27 (srli, I, comparator_14_eq, comparator_17_eq);
  and and_28 (srai, I, comparator_14_eq, comparator_19_eq);
  and and_29 (ori, I, comparator_15_eq);
  and and_30 (andi, I, comparator_16_eq);
  and and_31 (beq, ImmSel[2], comparator_9_eq);
  and and_32 (bne, ImmSel[2], comparator_10_eq);
  and and_33 (blt, ImmSel[2], comparator_13_eq);
  and and_34 (BrUn, ImmSel[2], comparator_15_eq);
  or or_2 (ImmSel[0], I_Load, I, I_jalr);
  nor nor_1 (RegWEn, ImmSel[1], beq, bne, blt, BrUn);
  or or_3 (or_3_out, I_Load, I_jalr, ImmSel[4], ImmSel[1], add, addi, ImmSel[2]);
  or or_4 (or_4_out, and_1080616f, andi);
  or or_5 (or_5_out, or_483976f9, ori);
  or or_6 (or_6_out, xor_e25a1cfa, xori);
  or or_7 (or_7_out, srli, srl_04da4a0d);
  or or_8 (or_8_out, slli, sll_a5a2ae92);
  or or_9 (or_9_out, slt, slti);
  assign bit_extender_1_out = {{3{ImmSel[3]}}, ImmSel[3]};  // Bit_Extender bit_extender_1
  or or_10 (or_10_out, R, I);
  or or_11 (or_11_out, lb, lh, lw);
  or or_12 (or_12_out, ImmSel[4], I_jalr);
  assign bit_extender_2_out = {{3{or_3_out}}, or_3_out};  // Bit_Extender bit_extender_2
  assign bit_extender_3_out = {{3{or_4_out}}, or_4_out};  // Bit_Extender bit_extender_3
  assign bit_extender_4_out = {{3{or_5_out}}, or_5_out};  // Bit_Extender bit_extender_4
  assign bit_extender_5_out = {{3{or_6_out}}, or_6_out};  // Bit_Extender bit_extender_5
  assign bit_extender_6_out = {{3{or_7_out}}, or_7_out};  // Bit_Extender bit_extender_6
  assign bit_extender_7_out = {{3{srai}}, srai};  // Bit_Extender bit_extender_7
  assign bit_extender_8_out = {{3{or_8_out}}, or_8_out};  // Bit_Extender bit_extender_8
  assign bit_extender_9_out = {{3{or_9_out}}, or_9_out};  // Bit_Extender bit_extender_9
  assign bit_extender_10_out = {{3{div}}, div};  // Bit_Extender bit_extender_10
  assign bit_extender_11_out = {{3{rem_90254230}}, rem_90254230};  // Bit_Extender bit_extender_11
  assign bit_extender_12_out = {{3{mul}}, mul};  // Bit_Extender bit_extender_12
  assign bit_extender_13_out = {{3{mulh}}, mulh};  // Bit_Extender bit_extender_13
  assign bit_extender_14_out = {{3{sub}}, sub};  // Bit_Extender bit_extender_14
  not not_1 (BSel, R);
  assign bit_extender_15_out = {{1{or_10_out}}, or_10_out};  // Bit_Extender bit_extender_15
  assign and_35_out = bit_extender_15_out & 2'b00;  // AND_Gate and_35, 2 bits wide
  assign bit_extender_16_out = {{1{or_11_out}}, or_11_out};  // Bit_Extender bit_extender_16
  assign and_36_out = bit_extender_16_out & 2'b01;  // AND_Gate and_36, 2 bits wide
  assign bit_extender_17_out = {{1{or_12_out}}, or_12_out};  // Bit_Extender bit_extender_17
  assign and_37_out = bit_extender_17_out & 2'b10;  // AND_Gate and_37, 2 bits wide
  assign and_38_out = bit_extender_2_out & 4'b0000;  // AND_Gate and_38, 4 bits wide
  assign and_39_out = bit_extender_3_out & 4'b0001;  // AND_Gate and_39, 4 bits wide
  assign and_40_out = bit_extender_4_out & 4'b0010;  // AND_Gate and_40, 4 bits wide
  assign and_41_out = bit_extender_5_out & 4'b0011;  // AND_Gate and_41, 4 bits wide
  assign and_42_out = bit_extender_6_out & 4'b0100;  // AND_Gate and_42, 4 bits wide
  assign and_43_out = bit_extender_7_out & 4'b0101;  // AND_Gate and_43, 4 bits wide
  assign and_44_out = bit_extender_8_out & 4'b0110;  // AND_Gate and_44, 4 bits wide
  assign and_45_out = bit_extender_9_out & 4'b0111;  // AND_Gate and_45, 4 bits wide
  assign and_46_out = bit_extender_10_out & 4'b1000;  // AND_Gate and_46, 4 bits wide
  assign and_47_out = bit_extender_11_out & 4'b1001;  // AND_Gate and_47, 4 bits wide
  assign and_48_out = bit_extender_12_out & 4'b1010;  // AND_Gate and_48, 4 bits wide
  assign and_49_out = bit_extender_13_out & 4'b1011;  // AND_Gate and_49, 4 bits wide
  assign and_50_out = bit_extender_14_out & 4'b1100;  // AND_Gate and_50, 4 bits wide
  assign and_51_out = bit_extender_1_out & 4'b1101;  // AND_Gate and_51, 4 bits wide
  or or_13 (ASel, beq, bne, blt, BrUn, ImmSel[3], ImmSel[4]);
  assign WBSel = and_35_out | and_36_out | and_37_out;  // OR_Gate or_14, 2 bits wide
  assign ALUSel = and_38_out | and_39_out | and_40_out | and_41_out | and_42_out | and_43_out | and_44_out | and_45_out | and_46_out | and_47_out | and_48_out | and_49_out | and_50_out | and_51_out;  // OR_Gate or_15, 4 bits wide

  assign MemRW = ImmSel[1];

  // Other names for the same wires on the sheet: A_select = ASel; ALU_select[3:0] = ALUSel; B_select = BSel;
  //   branch_equal = BrEq; branch_less_than = BrLt; bltu = BrUn; branch_unsigned = BrUn;
  //   immediate_value_select[4:0] = ImmSel; memory_read_write = ImmSel[1]; S_sw = ImmSel[1]; SB = ImmSel[2];
  //   U_lui = ImmSel[3]; UJ_jal = ImmSel[4]; instruction[31:0] = inst; opcode[6:0] = inst[6:0];
  //   funct3[2:0] = inst[14:12]; funct7[6:0] = inst[31:25]; PC_select = PCSel; reg_write_enable = RegWEn;
  //   write_back_select[1:0] = WBSel

  // Notes on the sheet:
  //   Type
  //   Check
  //   0 PC继续自增, 1 PC改为ALU的输出值
  //   寄存器允许写入
  //   因为不同的指令类型imm有分段
  //   是否以无符号模式比较
  //   0 从rs1输入, 1 从PC输入
  //   0 从rs2输入, 1 从立即数输入
  //   alu模式
  //   DRAM读写
  //   0 从alu输入, 1 从wb输入, 2 从PC输入
  //   I_Load有多个指令
  //   到ALU
  //   类型下只有一个指令的直接用opcode检测了
  //   到Reg File
  //   所以根据对应的指令type进行对应的解析处理
  //   unsigned
  //   没有实现div(带负数的除法)
  //   div R  funct3 0x4 funct7 0x01
  //   rem R funct3 0x6 funct7 0x01
  //   配合我的奇怪设计imm_gen
  //   lb, lh, lw是1(WB)
  //   R和I全是0 (ALU输入) 
  //   UJ_jal和I_jalr是2(PC)
  //   lui好像不需要这个
  //   建议去掉
  //   0000
  //   0000
  //   0000
  //   0000
  //   0000
  //   0000
  //   0000
  //   0000
  //   0000
  //   0000
  //   0000
  //   0000
  //   0010
  //   0011
  //   0011
  //   0110
  //   0001
  //   0001
  //   0010
  //   0100
  //   0100
  //   0101
  //   0110
  //   0111
  //   0111
  //   1000
  //   1001
  //   1010
  //   1011
  //   1100
  //   1101
endmodule
